# Fritzing sketch circuit (saved by Fritzing 0.9.9b)
circuit board: 6.88566cm x 5.36311cm
breadboards: 1

parts:
  Part1 = Arduino Uno (Rev3)
  R1 = Resistor [tolerance=±5% power=0.25 resistance=220 package=THT]
  LED1 = LED - 5mm [color="Green (570nm)" current=0.030 package="5 mm [THT]"]
  J1 = female pin header, 5 pins [form="♀ (female)"]

nets:
  N1: Part1.D13/SCK, R1.Pin_0, R1.Pin_1, LED1.anode
  N2: Part1.D2, J1.pin2
  N3: Part1.D3_PWM, J1.pin3
  N4: Part1.5V, J1.pin5
  N5: Part1.GND, LED1.cathode, J1.pin4
